# Fritzing sketch OpenTherm PCB (saved by Fritzing 0.9.3b)
circuit board: 3.90163cm x 1.84778cm
breadboards: 1

parts:
  J1 = Camdenboss CTB0158-2 [part_number=CTB0158-2 package=THT]
  D9 = Diode [package=diode-1n4001]
  Q2 = NPN-Transistor [package="TO92 [THT]"]
  R4 = Resistor [tolerance=±5% resistance=220 package=THT]
  R5 = Resistor [tolerance=±5% resistance=100 package=THT]
  D10 = Diode [package=diode-1n4001]
  D11 = Diode [package=diode-1n4001]
  R6 = Resistor [tolerance=±5% resistance=330 package=THT]
  U5 = Sharp PC817 [package=THT]
  U6 = Sharp PC817 [package=THT]
  D12 = Diode [package=diode-1n4148]
  D13 = Diode [package=diode-1n4148]
  D14 = Diode [package=diode-1n4148]
  D15 = Diode [package=diode-1n4148]
  Q3 = NPN-Transistor [package="TO92 [THT]"]
  R7 = Resistor [tolerance=±5% resistance=510 package=THT]
  R8 = Resistor [tolerance=±5% resistance=1k package=THT]
  R9 = Resistor [tolerance=±5% resistance=330 package=THT]
  J7 = female pin header, 5 pins [form="♀ (female)"]

nets:
  N1: J1.pin1, D12.C
  N2: J1.pin2, D13.C
  N3: D9.A, R5.Pin_1, D10.A, D11.A, U6.Pin_2, D12.A, D13.A
  N4: Q2.E, R4.Pin_1
  N5: Q2.B, D10.C, R6.Pin_0, U5.Pin_4
  N6: R4.Pin_0, R5.Pin_0, U6.Pin_1
  N7: D11.C, U5.Pin_3
  N8: R6.Pin_1, D14.C, D15.C
  N9: U5.Pin_1, R8.Pin_0
  N10: U5.Pin_2, Q3.C, R9.Pin_1, J7.pin1
  N11: U6.Pin_4, Q3.E, J7.pin4
  N12: U6.Pin_3, R9.Pin_0, J7.pin5
  N13: Q3.B, J7.pin2
  N14: R7.Pin_0, J7.pin3
  N15: R7.Pin_1, R8.Pin_1

notes:
  VCC
  IN
  OUT
  TMP
  GND
  OT1
  OT2
  1N4148
  4V7
  330Ω
  220Ω
  100Ω
  15V
  4V3
  1KΩ
  510Ω
  BC558B
  SENSOR
  -
  +
  !
